# Fritzing sketch esp-01_arduino_ideSketch (saved by Fritzing 0.9.4)
breadboards: 1

parts:
  S1 = Pushbutton [package="[THT]"]
  S2 = Pushbutton [package="[THT]"]
  LED1 = LED - 5mm [color="Blue (525nm)" package="5 mm [THT]"]
  R2 = Resistor [tolerance=±5% resistance=220 package=THT]
  U1 = ESP8266 WiFi Module [part_number=ESP8266]
  Part1 = FTDI Basic Programmer
  R4 = Resistor [tolerance=±5% resistance=470 package=THT]
  R5 = Resistor [tolerance=±5% resistance=220 package=THT]
  R6 = Resistor [tolerance=±5% resistance=220 package=THT]

nets:
  N1: S1.Pin_1, S1.Pin_2, U1.RST, R6.Pin_0
  GND: S1.Pin_3, S1.Pin_4, S2.Pin_3, S2.Pin_4, LED1.cathode, U1.GND, Part1.GND
  N2: S2.Pin_1, S2.Pin_2, R2.Pin_0, U1.GPIO_0
  N3: LED1.anode, R4.Pin_0
  N4: R2.Pin_1, U1.VCC, Part1.POWER, R5.Pin_1, R6.Pin_1
  N5: U1.RXD, Part1.TXO
  N6: U1.GPIO_2, R4.Pin_1
  N7: U1.TXD, Part1.RXI

notes:
  reset
  program

custom parts:
  ESP8266 WiFi Module: Generic WiFi Module based on the ESP8266 with onboard PCB antenna and UART communications
